# Fritzing sketch led13 (saved by Fritzing 0.9.4)
breadboards: 1

parts:
  R1 = Resistor [tolerance=±5% resistance=220 package=THT]
  Part4 = Arduino Uno (Rev3)
  LED2 = smd LED [color="Red (633nm)" package="0805 [SMD]"]

nets:
  N1: R1.Pin_0, Part4.GND
  N2: R1.Pin_1, LED2.cathode
  N3: Part4.D13/SCK, LED2.anode
